# Fritzing sketch North (saved by Fritzing 0.9.3b)
breadboards: 1

parts:
  Part1 = LSM303C (6 DOF)
  Part2 = Arduino Uno (Rev3) - ICSP

nets:
  GND: Part1.GND, Part2.GND
  N1: Part1.SDA/SDI/SDO, Part2.A4/SDA
  N2: Part1.SCL/SCLK, Part2.A5/SCL
