# Fritzing sketch 1bitdac_euro (saved by Fritzing 0.9.3b)
circuit board: 5.89805cm x 5.1582cm
perfboards: 1

parts:
  10kPot = Resistor [tolerance=±5% resistance=10k part_number=10kPot package=THT]
  wiper = Resistor [tolerance=±5% resistance=220 package=THT]
  10uF_El = Capacitor Polarized [package=cpol-radial-100uf-25v]
  120Ω = Resistor [tolerance=±5% resistance=220 package=THT]
  LM386 = LM386 [package=dip08]
  +5 = Antenna
  Lin = Antenna
  10Ω = Resistor [tolerance=±5% resistance=220 package=THT]
  68nK63 = Resonator [frequency="16 Mhz" package=THT]
  Common = Antenna
  220uF_El = Capacitor Polarized [package=cpol-radial-100uf-25v]
  Lout = Antenna
  47k63 = Film/Foil Capacitor [capacitance=100nF voltage=35V package="7.5mm [THT, pp]"]
  GND = Antenna
  10kPot1 = Resistor [tolerance=±5% resistance=10k part_number=10kPot package=THT]
  wiper1 = Resistor [tolerance=±5% resistance=220 package=THT]
  10uF_El1 = Capacitor Polarized [package=cpol-radial-100uf-25v]
  220uF = Capacitor Polarized [package=cpol-radial-100uf-25v]
  120Ω_2 = Resistor [tolerance=±5% resistance=220 package=THT]
  10Ω_2 = Resistor [tolerance=±5% resistance=220 package=THT]
  LM387 = LM386 [package=dip08]
  Rout = Antenna
  Rin = Antenna
  68nK64 = Resonator [frequency="16 Mhz" package=THT]
  47k63_2 = Film/Foil Capacitor [capacitance=100nF voltage=35V package="7.5mm [THT, pp]"]

nets:
  N1: 10kPot.Pin_0, LM386.-IN, LM386.V-, 10Ω.Pin_1, Common.antenna_lead, 47k63.+
  N2: 10kPot.Pin_1, 10uF_El.+
  N3: wiper.Pin_1, LM386.+IN
  N4: 10uF_El.-, 120Ω.Pin_0
  N5: 120Ω.Pin_1, Lin.antenna_lead, 47k63.-
  N6: LM386.GAIN, 68nK63.0
  N7: LM386.OUT, 220uF_El.+
  N8: LM386.V+, +5.antenna_lead, LM387.V+
  N9: 10Ω.Pin_0, 68nK63.1
  N10: 220uF_El.-, Lout.antenna_lead
  N11: GND.antenna_lead, 10kPot1.Pin_0, 10Ω_2.Pin_1, LM387.-IN, LM387.V-, 47k63_2.+
  N12: 10kPot1.Pin_1, 10uF_El1.+
  N13: wiper1.Pin_1, LM387.+IN
  N14: 10uF_El1.-, 120Ω_2.Pin_0
  N15: 220uF.+, LM387.OUT
  N16: 220uF.-, Rout.antenna_lead
  N17: 120Ω_2.Pin_1, Rin.antenna_lead, 47k63_2.-
  N18: 10Ω_2.Pin_0, 68nK64.1
  N19: LM387.GAIN, 68nK64.0

notes:
  Euro Parts
